// Logisim project circuito_atual.circ as structural Verilog: 28 circuits, main circuit ULA 32 Bits
module main (
);

  soma_1_bit soma_1_bit_1 ();  // open: SOMA, VAI_1, A, B, VEM_1
endmodule

module mux_8_bits_8canais (
  input  Canal_0,
  input  Canal_1,
  input  Canal_2,
  input  Canal_3,
  input  Canal_4,
  input  Canal_5,
  input  Canal_6,
  input  Canal_7,
  input  Sel_2,
  input  Sel_1,
  input  Sel_0,
  output S
);

  wire and_1_out, and_2_out, and_3_out, and_4_out, and_5_out, and_6_out, and_7_out, and_8_out;

  and and_1 (and_1_out, Canal_0, ~Sel_2, ~Sel_1, ~Sel_0);  // AND_Gate
  and and_2 (and_2_out, Canal_1, ~Sel_2, ~Sel_1, Sel_0);  // AND_Gate
  and and_3 (and_3_out, Canal_2, ~Sel_2, Sel_1, ~Sel_0);  // AND_Gate
  and and_4 (and_4_out, Canal_3, ~Sel_2, Sel_1, Sel_0);  // AND_Gate
  and and_5 (and_5_out, Canal_4, Sel_2, ~Sel_1, ~Sel_0);  // AND_Gate
  and and_6 (and_6_out, Canal_5, Sel_2, ~Sel_1, Sel_0);  // AND_Gate
  and and_7 (and_7_out, Canal_6, Sel_2, Sel_1, ~Sel_0);  // AND_Gate
  and and_8 (and_8_out, Canal_7, Sel_2, Sel_1, Sel_0);
  or or_1 (S, and_1_out, and_2_out, and_3_out, and_4_out, and_5_out, and_6_out, and_7_out, and_8_out);
endmodule

module mux2 (
  input  Canal_0,
  input  Canal_1,
  input  Sel_0,
  output out_4
);

  wire and_1_out, and_2_out;

  and and_1 (and_1_out, ~Sel_0, Canal_0);  // AND_Gate
  and and_2 (and_2_out, Sel_0, Canal_1);
  or or_1 (out_4, and_1_out, and_2_out);
endmodule

module mux_16 (
  input  Canal_0,
  input  Canal_1,
  input  Canal_2,
  input  Canal_3,
  input  Canal_4,
  input  Canal_5,
  input  Canal_6,
  input  Canal_7,
  input  Canal_8,
  input  Canal_9,
  input  Canal_10,
  input  Canal_11,
  input  Canal_12,
  input  Canal_13,
  input  Canal_14,
  input  Canal_15,
  input  in_17,
  input  in_18,
  input  in_19,
  input  in_20,
  output out_21
);

  wire mux_8_bits_8canais_1_s, mux_8_bits_8canais_2_s;

  mux_8_bits_8canais mux_8_bits_8canais_1 (
    .Canal_0(Canal_0), .Canal_1(Canal_1), .Canal_2(Canal_2), .Canal_3(Canal_3), .Canal_4(Canal_4),
    .Canal_5(Canal_5), .Canal_6(Canal_6), .Canal_7(Canal_7), .Sel_2(in_18), .Sel_1(in_19), .Sel_0(in_20),
    .S(mux_8_bits_8canais_1_s));
  mux_8_bits_8canais mux_8_bits_8canais_2 (
    .Canal_0(Canal_8), .Canal_1(Canal_9), .Canal_2(Canal_10), .Canal_3(Canal_11), .Canal_4(Canal_12),
    .Canal_5(Canal_13), .Canal_6(Canal_14), .Canal_7(Canal_15), .Sel_2(in_18), .Sel_1(in_19), .Sel_0(in_20),
    .S(mux_8_bits_8canais_2_s));
  mux2 mux2_1 (.Canal_0(mux_8_bits_8canais_1_s), .Canal_1(mux_8_bits_8canais_2_s), .Sel_0(in_17), .out_4(out_21));
endmodule

module ula_1_bit (
  input  A,
  input  B,
  input  Te,
  input  [3:0] Seletor,
  output \Saída ,
  output Ts
);

  wire and_1_out, nand_1_out, or_1_out, somador_completo_1_soma, xor_1_out;

  Somador_Completo somador_completo_1 (.out_5(Ts), .in_3(Te), .Soma(somador_completo_1_soma), .A(A), .B(B));
  and and_1 (and_1_out, A, B);
  or or_1 (or_1_out, A, B);
  xor xor_1 (xor_1_out, A, B);
  nand nand_1 (nand_1_out, A, B);
  mux_16 mux_16_1 (
    .Canal_0(and_1_out), .Canal_1(or_1_out), .Canal_2(xor_1_out), .Canal_3(somador_completo_1_soma),
    .Canal_9(nand_1_out), .in_17(Seletor[3]), .in_18(Seletor[2]), .in_19(Seletor[1]), .in_20(Seletor[0]),
    .out_21(\Saída ));  // open: Canal_4, Canal_5, Canal_6, Canal_7, Canal_8, Canal_10, Canal_11, Canal_12, Canal_13, Canal_14, Canal_15

  // Notes on the sheet:
  //   Trasnporte de entrada: Vai 1
  //   Transporte de saída: 
  //   Ula de 1 bit com porta nand
  //   Adição da porta NAND
  //   Parte Aritmética
  //   Parte lógica
  //   Porta Nand
  //   Tanto o te quando o ts são o mesmo vai 1, no entanto, o te está chegando, e o ts está saindo para a próxima operação no próximo bit
  //   000: AND
  //   001: OR
  //   010: NOR
  //   011: SOMA
  //   0101: SLL
  //   0110: SRL
  //   0111: SRA
  //   1001: NAND
  //   1010: LUA
  //   0100: SUBTRATOR
endmodule

module soma_1_bit (
  input  A,
  input  B,
  input  VEM_1,
  output SOMA,
  output VAI_1
);

  wire and_1_out, and_2_out, and_3_out, xor_1_out;

  xor xor_1 (xor_1_out, B, A);
  and and_1 (and_1_out, A, VEM_1);
  and and_2 (and_2_out, A, B);
  and and_3 (and_3_out, B, VEM_1);
  xor xor_2 (SOMA, xor_1_out, VEM_1);
  or or_1 (VAI_1, and_1_out, and_2_out, and_3_out);
  mux_16 mux_16_1 ();  // open: Canal_0, Canal_1, Canal_2, Canal_3, Canal_4, Canal_5, Canal_6, Canal_7, Canal_8, Canal_9, Canal_10, Canal_11, Canal_12, Canal_13, Canal_14, Canal_15, in_17, in_18, in_19, in_20, out_21
endmodule

module \mux_de_8_nova_versão  (
  input  Canal_0,
  input  Canal_1,
  input  Canal_2,
  input  Canal_3,
  input  Canal_4,
  input  Canal_5,
  input  Canal_6,
  input  Canal_7,
  input  Seletor_2,
  input  Seletor_1,
  input  Seletor_0,
  output \Saída 
);

  wire mux2_1_out_4, mux2_3_out_4, mux2_4_out_4, mux2_5_out_4, mux2_6_out_4;

  mux2 mux2_1 (.Canal_0(Canal_0), .Canal_1(Canal_1), .Sel_0(Seletor_0), .out_4(mux2_1_out_4));
  mux2 mux2_2 (.Canal_0(Canal_2), .Canal_1(Canal_3), .Sel_0(Seletor_0), .out_4(Seletor_0));
  mux2 mux2_3 (.Canal_0(Canal_4), .Canal_1(Canal_5), .Sel_0(Seletor_0), .out_4(mux2_3_out_4));
  mux2 mux2_4 (.Canal_0(Canal_6), .Canal_1(Canal_7), .Sel_0(Seletor_0), .out_4(mux2_4_out_4));
  mux2 mux2_5 (.Canal_0(mux2_1_out_4), .Canal_1(Seletor_0), .Sel_0(Seletor_1), .out_4(mux2_5_out_4));
  mux2 mux2_6 (.Canal_0(mux2_3_out_4), .Canal_1(mux2_4_out_4), .Sel_0(Seletor_1), .out_4(mux2_6_out_4));
  mux2 mux2_7 (.Canal_0(mux2_5_out_4), .Canal_1(mux2_6_out_4), .Sel_0(Seletor_2), .out_4(\Saída ));
endmodule

module Somador_Completo (
  input  A,
  input  B,
  input  in_3,
  output Soma,
  output out_5
);

  wire and_1_out, and_2_out, and_3_out, xor_1_out;

  or or_1 (out_5, and_1_out, and_2_out, and_3_out);
  and and_1 (and_1_out, A, B);
  and and_2 (and_2_out, in_3, B);
  and and_3 (and_3_out, in_3, A);
  xor xor_1 (xor_1_out, A, B);
  xor xor_2 (Soma, in_3, xor_1_out);

  // Notes on the sheet:
  //   S = (A Xor B) Xor Te
  //   Ts = (B*te) + (A + B) + (A*Te)
endmodule

module ULA_32_Bits (
  input  [31:0] A,
  input  [31:0] B,
  input  [3:0] Opercode,
  output [31:0] \Saída 
);

  wire ula_1_bit_1_ts, ula_1_bit_2_ts, ula_1_bit_3_ts, ula_1_bit_4_ts, ula_1_bit_5_ts, ula_1_bit_6_ts,
       ula_1_bit_7_ts, ula_1_bit_8_ts, ula_1_bit_9_ts, ula_1_bit_10_ts, ula_1_bit_11_ts, ula_1_bit_12_ts,
       ula_1_bit_13_ts, ula_1_bit_14_ts, ula_1_bit_15_ts, ula_1_bit_16_ts, ula_1_bit_17_ts, ula_1_bit_18_ts,
       ula_1_bit_19_ts, ula_1_bit_20_ts, ula_1_bit_21_ts, ula_1_bit_22_ts, ula_1_bit_23_ts, ula_1_bit_24_ts,
       ula_1_bit_25_ts, ula_1_bit_26_ts, ula_1_bit_27_ts, ula_1_bit_28_ts, ula_1_bit_29_ts, ula_1_bit_30_ts,
       ula_1_bit_31_ts;

  ula_1_bit ula_1_bit_1 (.Ts(ula_1_bit_1_ts), .Te(1'b0), .A(A[0]), .B(B[0]), .Seletor(Opercode), .\Saída (\Saída [0]));
  ula_1_bit ula_1_bit_2 (
    .Ts(ula_1_bit_2_ts), .Te(ula_1_bit_31_ts), .A(A[16]), .B(B[16]), .Seletor(Opercode), .\Saída (\Saída [16]));
  ula_1_bit ula_1_bit_3 (
    .Ts(ula_1_bit_3_ts), .Te(ula_1_bit_1_ts), .A(A[1]), .B(B[1]), .Seletor(Opercode), .\Saída (\Saída [1]));
  ula_1_bit ula_1_bit_4 (
    .Ts(ula_1_bit_4_ts), .Te(ula_1_bit_2_ts), .A(A[17]), .B(B[17]), .Seletor(Opercode), .\Saída (\Saída [17]));
  ula_1_bit ula_1_bit_5 (
    .Ts(ula_1_bit_5_ts), .Te(ula_1_bit_3_ts), .A(A[2]), .B(B[2]), .Seletor(Opercode), .\Saída (\Saída [2]));
  ula_1_bit ula_1_bit_6 (
    .Ts(ula_1_bit_6_ts), .Te(ula_1_bit_4_ts), .A(A[18]), .B(B[18]), .Seletor(Opercode), .\Saída (\Saída [18]));
  ula_1_bit ula_1_bit_7 (
    .Ts(ula_1_bit_7_ts), .Te(ula_1_bit_5_ts), .A(A[3]), .B(B[3]), .Seletor(Opercode), .\Saída (\Saída [3]));
  ula_1_bit ula_1_bit_8 (
    .Ts(ula_1_bit_8_ts), .Te(ula_1_bit_6_ts), .A(A[19]), .B(B[19]), .Seletor(Opercode), .\Saída (\Saída [19]));
  ula_1_bit ula_1_bit_9 (
    .Ts(ula_1_bit_9_ts), .Te(ula_1_bit_7_ts), .A(A[4]), .B(B[4]), .Seletor(Opercode), .\Saída (\Saída [4]));
  ula_1_bit ula_1_bit_10 (
    .Ts(ula_1_bit_10_ts), .Te(ula_1_bit_8_ts), .A(A[20]), .B(B[20]), .Seletor(Opercode), .\Saída (\Saída [20]));
  ula_1_bit ula_1_bit_11 (
    .Ts(ula_1_bit_11_ts), .Te(ula_1_bit_9_ts), .A(A[5]), .B(B[5]), .Seletor(Opercode), .\Saída (\Saída [5]));
  ula_1_bit ula_1_bit_12 (
    .Ts(ula_1_bit_12_ts), .Te(ula_1_bit_10_ts), .A(A[21]), .B(B[21]), .Seletor(Opercode),
    .\Saída (\Saída [21]));
  ula_1_bit ula_1_bit_13 (
    .Ts(ula_1_bit_13_ts), .Te(ula_1_bit_11_ts), .A(A[6]), .B(B[6]), .Seletor(Opercode), .\Saída (\Saída [6]));
  ula_1_bit ula_1_bit_14 (
    .Ts(ula_1_bit_14_ts), .Te(ula_1_bit_12_ts), .A(A[22]), .B(B[22]), .Seletor(Opercode),
    .\Saída (\Saída [22]));
  ula_1_bit ula_1_bit_15 (
    .Ts(ula_1_bit_15_ts), .Te(ula_1_bit_13_ts), .A(A[7]), .B(B[7]), .Seletor(Opercode), .\Saída (\Saída [7]));
  ula_1_bit ula_1_bit_16 (
    .Ts(ula_1_bit_16_ts), .Te(ula_1_bit_14_ts), .A(A[23]), .B(B[23]), .Seletor(Opercode),
    .\Saída (\Saída [23]));
  ula_1_bit ula_1_bit_17 (
    .Ts(ula_1_bit_17_ts), .Te(ula_1_bit_15_ts), .A(A[8]), .B(B[8]), .Seletor(Opercode), .\Saída (\Saída [8]));
  ula_1_bit ula_1_bit_18 (
    .Ts(ula_1_bit_18_ts), .Te(ula_1_bit_16_ts), .A(A[24]), .B(B[24]), .Seletor(Opercode),
    .\Saída (\Saída [24]));
  ula_1_bit ula_1_bit_19 (
    .Ts(ula_1_bit_19_ts), .Te(ula_1_bit_17_ts), .A(A[9]), .B(B[9]), .Seletor(Opercode), .\Saída (\Saída [9]));
  ula_1_bit ula_1_bit_20 (
    .Ts(ula_1_bit_20_ts), .Te(ula_1_bit_18_ts), .A(A[25]), .B(B[25]), .Seletor(Opercode),
    .\Saída (\Saída [25]));
  ula_1_bit ula_1_bit_21 (
    .Ts(ula_1_bit_21_ts), .Te(ula_1_bit_19_ts), .A(A[10]), .B(B[10]), .Seletor(Opercode),
    .\Saída (\Saída [10]));
  ula_1_bit ula_1_bit_22 (
    .Ts(ula_1_bit_22_ts), .Te(ula_1_bit_20_ts), .A(A[26]), .B(B[26]), .Seletor(Opercode),
    .\Saída (\Saída [26]));
  ula_1_bit ula_1_bit_23 (
    .Ts(ula_1_bit_23_ts), .Te(ula_1_bit_21_ts), .A(A[11]), .B(B[11]), .Seletor(Opercode),
    .\Saída (\Saída [11]));
  ula_1_bit ula_1_bit_24 (
    .Ts(ula_1_bit_24_ts), .Te(ula_1_bit_22_ts), .A(A[27]), .B(B[27]), .Seletor(Opercode),
    .\Saída (\Saída [27]));
  ula_1_bit ula_1_bit_25 (
    .Ts(ula_1_bit_25_ts), .Te(ula_1_bit_23_ts), .A(A[12]), .B(B[12]), .Seletor(Opercode),
    .\Saída (\Saída [12]));
  ula_1_bit ula_1_bit_26 (
    .Ts(ula_1_bit_26_ts), .Te(ula_1_bit_24_ts), .A(A[28]), .B(B[28]), .Seletor(Opercode),
    .\Saída (\Saída [28]));
  ula_1_bit ula_1_bit_27 (
    .Ts(ula_1_bit_27_ts), .Te(ula_1_bit_25_ts), .A(A[13]), .B(B[13]), .Seletor(Opercode),
    .\Saída (\Saída [13]));
  ula_1_bit ula_1_bit_28 (
    .Ts(ula_1_bit_28_ts), .Te(ula_1_bit_26_ts), .A(A[29]), .B(B[29]), .Seletor(Opercode),
    .\Saída (\Saída [29]));
  ula_1_bit ula_1_bit_29 (
    .Ts(ula_1_bit_29_ts), .Te(ula_1_bit_27_ts), .A(A[14]), .B(B[14]), .Seletor(Opercode),
    .\Saída (\Saída [14]));
  ula_1_bit ula_1_bit_30 (
    .Ts(ula_1_bit_30_ts), .Te(ula_1_bit_28_ts), .A(A[30]), .B(B[30]), .Seletor(Opercode),
    .\Saída (\Saída [30]));
  ula_1_bit ula_1_bit_31 (
    .Ts(ula_1_bit_31_ts), .Te(ula_1_bit_29_ts), .A(A[15]), .B(B[15]), .Seletor(Opercode),
    .\Saída (\Saída [15]));
  ula_1_bit ula_1_bit_32 (
    .Te(ula_1_bit_30_ts), .A(A[31]), .B(B[31]), .Seletor(Opercode), .\Saída (\Saída [31]));  // open: Ts

  // Other names for the same wires on the sheet: S0 = \Saída [0]; S1 = \Saída [1]; S2 = \Saída [2]; S3 = \Saída [3];
  //   S4 = \Saída [4]; S5 = \Saída [5]; S6 = \Saída [6]; S7 = \Saída [7]; S8 = \Saída [8]; S9 = \Saída [9];
  //   S10 = \Saída [10]; S11 = \Saída [11]; S12 = \Saída [12]; S13 = \Saída [13]; S14 = \Saída [14];
  //   S15 = \Saída [15]; S16 = \Saída [16]; S17 = \Saída [17]; S18 = \Saída [18]; S19 = \Saída [19];
  //   S20 = \Saída [20]; S21 = \Saída [21]; S22 = \Saída [22]; S23 = \Saída [23]; S24 = \Saída [24];
  //   S25 = \Saída [25]; S26 = \Saída [26]; S27 = \Saída [27]; S28 = \Saída [28]; S29 = \Saída [29];
  //   S30 = \Saída [30]; S31 = \Saída [31]
endmodule

module SLL_de_32_bits (
  input  [31:0] in_1,
  input  in_2,
  output [31:0] out_3
);

  Multiplexer #(.width(32), .enable("false")) multiplexer_1 (
    .in0(in_1), .in1({in_1[30:0], 1'b0}), .out(out_3), .sel(in_2));
endmodule

module ula_de_1_bit_sem_porta_nand (
  input  A,
  input  B,
  input  Transporte_de_entrada,
  input  [3:0] Seletor,
  output Resultado,
  output \Transporte_de_saída 
);

  wire and_1_out, or_1_out, somador_completo_1_soma, xor_1_out;

  Somador_Completo somador_completo_1 (
    .out_5(\Transporte_de_saída ), .in_3(Transporte_de_entrada), .Soma(somador_completo_1_soma), .A(A), .B(B));
  and and_1 (and_1_out, A, B);
  or or_1 (or_1_out, A, B);
  xor xor_1 (xor_1_out, A, B);
  mux_16 mux_16_1 (
    .Canal_0(and_1_out), .Canal_1(or_1_out), .Canal_2(xor_1_out), .Canal_3(somador_completo_1_soma),
    .in_17(Seletor[3]), .in_18(Seletor[2]), .in_19(Seletor[1]), .in_20(Seletor[0]), .out_21(Resultado));  // open: Canal_4, Canal_5, Canal_6, Canal_7, Canal_8, Canal_9, Canal_10, Canal_11, Canal_12, Canal_13, Canal_14, Canal_15

  // Notes on the sheet:
  //   Trasnporte de entrada: Vai 1
  //   Transporte de saída: 
  //   Ula de 1 bit sem porta nand
  //   Tanto o te quando o ts são o mesmo vai 1, no entanto, o te está chegando, e o ts está saindo para a próxima operação no próximo bit
endmodule

module Registrador_de_5_bits (
  input  [4:0] Porta_D,
  input  Clock,
  output [4:0] \Saída 
);

  wire undriven;

  D_Flip_Flop d_ff_1 (.clk(Clock), .D(Porta_D[4]), .Q(\Saída [4]));  // open: Qn, preset, en, reset
  D_Flip_Flop d_ff_2 (.clk(Clock), .D(Porta_D[3]), .Q(\Saída [3]));  // open: Qn, preset, en, reset
  D_Flip_Flop d_ff_3 (.clk(Clock), .D(Porta_D[2]), .Q(\Saída [2]));  // open: Qn, preset, en, reset
  D_Flip_Flop d_ff_4 (
    .clk(Clock), .D(Porta_D[1]), .Q(\Saída [1]), .preset(undriven), .en(undriven));  // open: Qn, reset
  D_Flip_Flop d_ff_5 (.clk(Clock), .D(Porta_D[0]), .Q(\Saída [0]));  // open: Qn, preset, en, reset

  // Notes on the sheet:
  //   Registrador de 5 bits
endmodule

module Registrador_de_32_bits (
  input  WR,
  input  Reset,
  input  [31:0] Entrada,
  output [31:0] \Saída 
);

  D_Flip_Flop d_ff_1 (.clk(Entrada[25]), .D(Entrada[15]), .Q(\Saída [15]), .reset(Reset));  // open: Qn, preset, en
  D_Flip_Flop d_ff_2 (.clk(Entrada[25]), .D(Entrada[31]), .Q(\Saída [31]), .reset(Reset));  // open: Qn, preset, en
  D_Flip_Flop d_ff_3 (.clk(Entrada[25]), .D(Entrada[14]), .Q(\Saída [14]), .reset(Reset));  // open: Qn, preset, en
  D_Flip_Flop d_ff_4 (.clk(Entrada[25]), .D(Entrada[30]), .Q(\Saída [30]), .reset(Reset));  // open: Qn, preset, en
  D_Flip_Flop d_ff_5 (.clk(Entrada[25]), .D(Entrada[13]), .Q(\Saída [13]), .reset(Reset));  // open: Qn, preset, en
  D_Flip_Flop d_ff_6 (.clk(Entrada[25]), .D(Entrada[29]), .Q(\Saída [29]), .reset(Reset));  // open: Qn, preset, en
  D_Flip_Flop d_ff_7 (.clk(Entrada[25]), .D(Entrada[12]), .Q(\Saída [12]), .reset(Reset));  // open: Qn, preset, en
  D_Flip_Flop d_ff_8 (.clk(Entrada[25]), .D(Entrada[28]), .Q(\Saída [28]), .reset(Reset));  // open: Qn, preset, en
  D_Flip_Flop d_ff_9 (.clk(Entrada[25]), .D(Entrada[11]), .Q(\Saída [11]), .reset(Reset));  // open: Qn, preset, en
  D_Flip_Flop d_ff_10 (.clk(Entrada[25]), .D(Entrada[27]), .Q(\Saída [27]), .reset(Reset));  // open: Qn, preset, en
  D_Flip_Flop d_ff_11 (.clk(Entrada[25]), .D(Entrada[10]), .Q(\Saída [10]), .reset(Reset));  // open: Qn, preset, en
  D_Flip_Flop d_ff_12 (.clk(Entrada[25]), .D(Entrada[26]), .Q(\Saída [26]), .reset(Reset));  // open: Qn, preset, en
  D_Flip_Flop d_ff_13 (.clk(Entrada[25]), .D(Entrada[9]), .Q(\Saída [9]), .reset(Reset));  // open: Qn, preset, en
  D_Flip_Flop d_ff_14 (.clk(Entrada[25]), .D(Entrada[25]), .Q(\Saída [25]), .reset(Reset));  // open: Qn, preset, en
  D_Flip_Flop d_ff_15 (.clk(Entrada[25]), .D(Entrada[8]), .Q(\Saída [8]), .reset(Reset));  // open: Qn, preset, en
  D_Flip_Flop d_ff_16 (.clk(Entrada[25]), .D(Entrada[24]), .Q(\Saída [24]), .reset(Reset));  // open: Qn, preset, en
  D_Flip_Flop d_ff_17 (.clk(Entrada[25]), .D(Entrada[7]), .Q(\Saída [7]), .reset(Reset));  // open: Qn, preset, en
  D_Flip_Flop d_ff_18 (.clk(Entrada[25]), .D(Entrada[23]), .Q(\Saída [23]), .reset(Reset));  // open: Qn, preset, en
  D_Flip_Flop d_ff_19 (.clk(Entrada[25]), .D(Entrada[6]), .Q(\Saída [6]), .reset(Reset));  // open: Qn, preset, en
  D_Flip_Flop d_ff_20 (.clk(Entrada[25]), .D(Entrada[22]), .Q(\Saída [22]), .reset(Reset));  // open: Qn, preset, en
  D_Flip_Flop d_ff_21 (.clk(Entrada[25]), .D(Entrada[5]), .Q(\Saída [5]), .reset(Reset));  // open: Qn, preset, en
  D_Flip_Flop d_ff_22 (.clk(Entrada[25]), .D(Entrada[21]), .Q(\Saída [21]), .reset(Reset));  // open: Qn, preset, en
  D_Flip_Flop d_ff_23 (.clk(Entrada[25]), .D(Entrada[4]), .Q(\Saída [4]), .reset(Reset));  // open: Qn, preset, en
  D_Flip_Flop d_ff_24 (.clk(Entrada[25]), .D(Entrada[20]), .Q(\Saída [20]), .reset(Reset));  // open: Qn, preset, en
  D_Flip_Flop d_ff_25 (
    .clk(Entrada[25]), .D(Entrada[3]), .Q(\Saída [3]), .en(Entrada[3]), .reset(Reset));  // open: Qn, preset
  D_Flip_Flop d_ff_26 (.clk(Entrada[25]), .D(Entrada[19]), .Q(\Saída [19]), .reset(Reset));  // open: Qn, preset, en
  D_Flip_Flop d_ff_27 (.clk(Entrada[25]), .D(Entrada[2]), .Q(\Saída [2]), .reset(Reset));  // open: Qn, preset, en
  D_Flip_Flop d_ff_28 (.clk(Entrada[25]), .D(Entrada[18]), .Q(\Saída [18]), .reset(Reset));  // open: Qn, preset, en
  D_Flip_Flop d_ff_29 (.clk(Entrada[25]), .D(Entrada[1]), .Q(\Saída [1]), .reset(Reset));  // open: Qn, preset, en
  D_Flip_Flop d_ff_30 (.clk(Entrada[25]), .D(Entrada[17]), .Q(\Saída [17]), .reset(Reset));  // open: Qn, preset, en
  D_Flip_Flop d_ff_31 (.clk(Entrada[25]), .D(Entrada[0]), .Q(\Saída [0]), .reset(Reset));  // open: Qn, preset, en
  D_Flip_Flop d_ff_32 (.clk(Entrada[25]), .D(Entrada[16]), .Q(Reset), .reset(Reset));  // open: Qn, preset, en

  assign \Saída [16] = Reset;
  assign WR = Entrada[25];
endmodule

module Banco_de_Registradores (
  input  [31:0] Data_in_Externo,
  input  [31:0] DataIn,
  input  in_3,
  input  WR,
  input  [4:0] SelRegA,
  input  [4:0] SelRegW,
  input  Reset,
  input  [4:0] SelRegB,
  output [31:0] DataRegA,
  output [31:0] DataRegB
);

  wire W0, W1, W2, W3, W4, W5, W6, W7, W8, W9, W10, W11, W12, W13, W14, W15, W16, W17, W18, W19, W20, W21,
       W22, W23, W24, W25, W26, W27, W28, W29, W30, W31;
  wire [31:0] multiplexer_1_out, \registrador_de_32_bits_1_saída , \registrador_de_32_bits_2_saída ,
       \registrador_de_32_bits_4_saída , \registrador_de_32_bits_5_saída , \registrador_de_32_bits_6_saída ,
       \registrador_de_32_bits_7_saída , \registrador_de_32_bits_8_saída , \registrador_de_32_bits_9_saída ,
       \registrador_de_32_bits_10_saída , \registrador_de_32_bits_11_saída ,
       \registrador_de_32_bits_12_saída , \registrador_de_32_bits_13_saída ,
       \registrador_de_32_bits_14_saída , \registrador_de_32_bits_15_saída ,
       \registrador_de_32_bits_16_saída , \registrador_de_32_bits_17_saída ,
       \registrador_de_32_bits_18_saída , \registrador_de_32_bits_19_saída ,
       \registrador_de_32_bits_20_saída , \registrador_de_32_bits_21_saída ,
       \registrador_de_32_bits_22_saída , \registrador_de_32_bits_23_saída ,
       \registrador_de_32_bits_24_saída , \registrador_de_32_bits_25_saída ,
       \registrador_de_32_bits_26_saída , \registrador_de_32_bits_27_saída ,
       \registrador_de_32_bits_28_saída , \registrador_de_32_bits_29_saída ,
       \registrador_de_32_bits_30_saída , \registrador_de_32_bits_31_saída ,
       \registrador_de_32_bits_32_saída ;

  Demultiplexer #(.select(5), .enable("false")) demultiplexer_1 (
    .out0(W0), .out1(W1), .out2(W2), .out3(W3), .out4(W4), .out5(W5), .out6(W6), .out7(W7), .out8(W8),
    .out9(W9), .out10(W10), .out11(W11), .out12(W12), .out13(W13), .out14(W14), .out15(W15), .out16(W16),
    .out17(W17), .out18(W18), .out19(W19), .out20(W20), .out21(W21), .out22(W22), .out23(W23), .out24(W24),
    .out25(W25), .out26(W26), .out27(W27), .out28(W28), .out29(W29), .out30(W30), .out31(W31), .in(WR),
    .sel(SelRegW));
  Multiplexer #(.width(32), .enable("false")) multiplexer_1 (
    .in0(Data_in_Externo), .in1(DataIn), .out(multiplexer_1_out), .sel(in_3));
  Registrador_de_32_bits registrador_de_32_bits_1 (
    .WR(W0), .Entrada(multiplexer_1_out), .\Saída (\registrador_de_32_bits_1_saída ));  // open: Reset
  Registrador_de_32_bits registrador_de_32_bits_2 (
    .WR(W4), .Entrada(multiplexer_1_out), .\Saída (\registrador_de_32_bits_2_saída ));  // open: Reset
  Registrador_de_32_bits registrador_de_32_bits_3 (
    .WR(W8), .Entrada(multiplexer_1_out), .\Saída (\registrador_de_32_bits_1_saída ));  // open: Reset
  Registrador_de_32_bits registrador_de_32_bits_4 (
    .WR(W12), .Entrada(multiplexer_1_out), .\Saída (\registrador_de_32_bits_4_saída ));  // open: Reset
  Registrador_de_32_bits registrador_de_32_bits_5 (
    .WR(W16), .Entrada(multiplexer_1_out), .\Saída (\registrador_de_32_bits_5_saída ));  // open: Reset
  Registrador_de_32_bits registrador_de_32_bits_6 (
    .WR(W20), .Entrada(multiplexer_1_out), .\Saída (\registrador_de_32_bits_6_saída ));  // open: Reset
  Registrador_de_32_bits registrador_de_32_bits_7 (
    .WR(W24), .Entrada(multiplexer_1_out), .\Saída (\registrador_de_32_bits_7_saída ));  // open: Reset
  Registrador_de_32_bits registrador_de_32_bits_8 (
    .WR(W28), .Entrada(multiplexer_1_out), .\Saída (\registrador_de_32_bits_8_saída ));  // open: Reset
  Registrador_de_32_bits registrador_de_32_bits_9 (
    .WR(W1), .Entrada(multiplexer_1_out), .\Saída (\registrador_de_32_bits_9_saída ));  // open: Reset
  Registrador_de_32_bits registrador_de_32_bits_10 (
    .WR(W5), .Entrada(multiplexer_1_out), .\Saída (\registrador_de_32_bits_10_saída ));  // open: Reset
  Registrador_de_32_bits registrador_de_32_bits_11 (
    .WR(W9), .Entrada(multiplexer_1_out), .\Saída (\registrador_de_32_bits_11_saída ));  // open: Reset
  Registrador_de_32_bits registrador_de_32_bits_12 (
    .WR(W13), .Entrada(multiplexer_1_out), .\Saída (\registrador_de_32_bits_12_saída ));  // open: Reset
  Registrador_de_32_bits registrador_de_32_bits_13 (
    .WR(W17), .Entrada(multiplexer_1_out), .\Saída (\registrador_de_32_bits_13_saída ));  // open: Reset
  Registrador_de_32_bits registrador_de_32_bits_14 (
    .WR(W21), .Entrada(multiplexer_1_out), .\Saída (\registrador_de_32_bits_14_saída ));  // open: Reset
  Registrador_de_32_bits registrador_de_32_bits_15 (
    .WR(W25), .Entrada(multiplexer_1_out), .\Saída (\registrador_de_32_bits_15_saída ));  // open: Reset
  Registrador_de_32_bits registrador_de_32_bits_16 (
    .WR(W29), .Entrada(multiplexer_1_out), .\Saída (\registrador_de_32_bits_16_saída ));  // open: Reset
  Registrador_de_32_bits registrador_de_32_bits_17 (
    .WR(W2), .Entrada(multiplexer_1_out), .\Saída (\registrador_de_32_bits_17_saída ));  // open: Reset
  Registrador_de_32_bits registrador_de_32_bits_18 (
    .WR(W6), .Entrada(multiplexer_1_out), .\Saída (\registrador_de_32_bits_18_saída ));  // open: Reset
  Registrador_de_32_bits registrador_de_32_bits_19 (
    .WR(W10), .Entrada(multiplexer_1_out), .\Saída (\registrador_de_32_bits_19_saída ));  // open: Reset
  Registrador_de_32_bits registrador_de_32_bits_20 (
    .WR(W14), .Entrada(multiplexer_1_out), .\Saída (\registrador_de_32_bits_20_saída ));  // open: Reset
  Registrador_de_32_bits registrador_de_32_bits_21 (
    .WR(W18), .Entrada(multiplexer_1_out), .\Saída (\registrador_de_32_bits_21_saída ));  // open: Reset
  Registrador_de_32_bits registrador_de_32_bits_22 (
    .WR(W22), .Entrada(multiplexer_1_out), .\Saída (\registrador_de_32_bits_22_saída ));  // open: Reset
  Registrador_de_32_bits registrador_de_32_bits_23 (
    .WR(W26), .Entrada(multiplexer_1_out), .\Saída (\registrador_de_32_bits_23_saída ));  // open: Reset
  Registrador_de_32_bits registrador_de_32_bits_24 (
    .WR(W30), .Entrada(multiplexer_1_out), .\Saída (\registrador_de_32_bits_24_saída ));  // open: Reset
  Registrador_de_32_bits registrador_de_32_bits_25 (
    .WR(W3), .Entrada(multiplexer_1_out), .\Saída (\registrador_de_32_bits_25_saída ));  // open: Reset
  Registrador_de_32_bits registrador_de_32_bits_26 (
    .WR(W7), .Entrada(multiplexer_1_out), .\Saída (\registrador_de_32_bits_26_saída ));  // open: Reset
  Registrador_de_32_bits registrador_de_32_bits_27 (
    .WR(W11), .Entrada(multiplexer_1_out), .\Saída (\registrador_de_32_bits_27_saída ));  // open: Reset
  Registrador_de_32_bits registrador_de_32_bits_28 (
    .WR(W15), .Entrada(multiplexer_1_out), .\Saída (\registrador_de_32_bits_28_saída ));  // open: Reset
  Registrador_de_32_bits registrador_de_32_bits_29 (
    .WR(W19), .Entrada(multiplexer_1_out), .\Saída (\registrador_de_32_bits_29_saída ));  // open: Reset
  Registrador_de_32_bits registrador_de_32_bits_30 (
    .WR(W23), .Entrada(multiplexer_1_out), .\Saída (\registrador_de_32_bits_30_saída ));  // open: Reset
  Registrador_de_32_bits registrador_de_32_bits_31 (
    .WR(W27), .Entrada(multiplexer_1_out), .\Saída (\registrador_de_32_bits_31_saída ));  // open: Reset
  Registrador_de_32_bits registrador_de_32_bits_32 (
    .WR(W31), .Entrada(multiplexer_1_out), .\Saída (\registrador_de_32_bits_32_saída ));  // open: Reset
  Multiplexer #(.select(5), .width(32), .enable("false")) multiplexer_2 (
    .in0({32{1'b0}}), .in1(\registrador_de_32_bits_9_saída ), .in2(\registrador_de_32_bits_17_saída ),
    .in3(\registrador_de_32_bits_25_saída ), .in4(\registrador_de_32_bits_2_saída ),
    .in5(\registrador_de_32_bits_10_saída ), .in6(\registrador_de_32_bits_18_saída ),
    .in7(\registrador_de_32_bits_26_saída ), .in8(\registrador_de_32_bits_1_saída ),
    .in9(\registrador_de_32_bits_11_saída ), .in10(\registrador_de_32_bits_19_saída ),
    .in11(\registrador_de_32_bits_27_saída ), .in12(\registrador_de_32_bits_4_saída ),
    .in13(\registrador_de_32_bits_12_saída ), .in14(\registrador_de_32_bits_20_saída ),
    .in15(\registrador_de_32_bits_28_saída ), .in16(\registrador_de_32_bits_5_saída ),
    .in17(\registrador_de_32_bits_13_saída ), .in18(\registrador_de_32_bits_21_saída ),
    .in19(\registrador_de_32_bits_29_saída ), .in20(\registrador_de_32_bits_6_saída ),
    .in21(\registrador_de_32_bits_14_saída ), .in22(\registrador_de_32_bits_22_saída ),
    .in23(\registrador_de_32_bits_30_saída ), .in24(\registrador_de_32_bits_7_saída ),
    .in25(\registrador_de_32_bits_15_saída ), .in26(\registrador_de_32_bits_23_saída ),
    .in27(\registrador_de_32_bits_31_saída ), .in28(\registrador_de_32_bits_8_saída ),
    .in29(\registrador_de_32_bits_16_saída ), .in30(\registrador_de_32_bits_24_saída ),
    .in31(\registrador_de_32_bits_32_saída ), .out(DataRegA), .sel(SelRegA));
  Multiplexer #(.select(5), .width(32), .enable("false")) multiplexer_3 (
    .in0({32{1'b0}}), .in1(\registrador_de_32_bits_9_saída ), .in2(\registrador_de_32_bits_17_saída ),
    .in3(\registrador_de_32_bits_25_saída ), .in4(\registrador_de_32_bits_2_saída ),
    .in5(\registrador_de_32_bits_10_saída ), .in6(\registrador_de_32_bits_18_saída ),
    .in7(\registrador_de_32_bits_26_saída ), .in8(\registrador_de_32_bits_1_saída ),
    .in9(\registrador_de_32_bits_11_saída ), .in10(\registrador_de_32_bits_19_saída ),
    .in11(\registrador_de_32_bits_27_saída ), .in12(\registrador_de_32_bits_4_saída ),
    .in13(\registrador_de_32_bits_12_saída ), .in14(\registrador_de_32_bits_20_saída ),
    .in15(\registrador_de_32_bits_28_saída ), .in16(\registrador_de_32_bits_5_saída ),
    .in17(\registrador_de_32_bits_13_saída ), .in18(\registrador_de_32_bits_21_saída ),
    .in19(\registrador_de_32_bits_29_saída ), .in20(\registrador_de_32_bits_6_saída ),
    .in21(\registrador_de_32_bits_14_saída ), .in22(\registrador_de_32_bits_22_saída ),
    .in23(\registrador_de_32_bits_30_saída ), .in24(\registrador_de_32_bits_7_saída ),
    .in25(\registrador_de_32_bits_15_saída ), .in26(\registrador_de_32_bits_23_saída ),
    .in27(\registrador_de_32_bits_31_saída ), .in28(\registrador_de_32_bits_8_saída ),
    .in29(\registrador_de_32_bits_16_saída ), .in30(\registrador_de_32_bits_24_saída ),
    .in31(\registrador_de_32_bits_32_saída ), .out(DataRegB), .sel(SelRegB));

  // Other names for the same wires on the sheet: R1 = Reset; R2 = Reset; R3 = Reset; R4 = Reset; R5 = Reset;
  //   R6 = Reset; R7 = Reset; R8 = Reset; R9 = Reset; R10 = Reset; R11 = Reset; R12 = Reset; R13 = Reset; R14 = Reset;
  //   R15 = Reset; R16 = Reset; R17 = Reset; R18 = Reset; R19 = Reset; R20 = Reset; R21 = Reset; R22 = Reset;
  //   R23 = Reset; R24 = Reset; R25 = Reset; R26 = Reset; R27 = Reset; R28 = Reset; R29 = Reset; R30 = Reset;
  //   R31 = Reset
endmodule

module Banco_de_Registradores_8_bits (
  input  WR,
  input  [4:0] Data_N,
  input  [2:0] in_3,
  input  [2:0] SelRegW,
  input  [2:0] in_5,
  output [4:0] DataRegA,
  output [4:0] DataRegB
);

  wire demultiplexer_1_out0, demultiplexer_1_out1, demultiplexer_1_out2, demultiplexer_1_out3,
       demultiplexer_1_out4, demultiplexer_1_out5, demultiplexer_1_out6, demultiplexer_1_out7;
  wire [4:0] \registrador_de_5_bits_1_saída , \registrador_de_5_bits_2_saída ,
       \registrador_de_5_bits_3_saída , \registrador_de_5_bits_4_saída , \registrador_de_5_bits_5_saída ,
       \registrador_de_5_bits_6_saída , \registrador_de_5_bits_7_saída , \registrador_de_5_bits_8_saída ;

  Demultiplexer #(.select(3), .enable("false")) demultiplexer_1 (
    .out0(demultiplexer_1_out0), .out1(demultiplexer_1_out1), .out2(demultiplexer_1_out2),
    .out3(demultiplexer_1_out3), .out4(demultiplexer_1_out4), .out5(demultiplexer_1_out5),
    .out6(demultiplexer_1_out6), .out7(demultiplexer_1_out7), .in(WR), .sel(SelRegW));
  Registrador_de_5_bits registrador_de_5_bits_1 (
    .Porta_D(Data_N), .Clock(demultiplexer_1_out0), .\Saída (\registrador_de_5_bits_1_saída ));
  Registrador_de_5_bits registrador_de_5_bits_2 (
    .Porta_D(Data_N), .Clock(demultiplexer_1_out1), .\Saída (\registrador_de_5_bits_2_saída ));
  Registrador_de_5_bits registrador_de_5_bits_3 (
    .Porta_D(Data_N), .Clock(demultiplexer_1_out2), .\Saída (\registrador_de_5_bits_3_saída ));
  Registrador_de_5_bits registrador_de_5_bits_4 (
    .Porta_D(Data_N), .Clock(demultiplexer_1_out3), .\Saída (\registrador_de_5_bits_4_saída ));
  Registrador_de_5_bits registrador_de_5_bits_5 (
    .Porta_D(Data_N), .Clock(demultiplexer_1_out4), .\Saída (\registrador_de_5_bits_5_saída ));
  Registrador_de_5_bits registrador_de_5_bits_6 (
    .Porta_D(Data_N), .Clock(demultiplexer_1_out5), .\Saída (\registrador_de_5_bits_6_saída ));
  Registrador_de_5_bits registrador_de_5_bits_7 (
    .Porta_D(Data_N), .Clock(demultiplexer_1_out6), .\Saída (\registrador_de_5_bits_7_saída ));
  Registrador_de_5_bits registrador_de_5_bits_8 (
    .Porta_D(Data_N), .Clock(demultiplexer_1_out7), .\Saída (\registrador_de_5_bits_8_saída ));
  Multiplexer #(.select(3), .width(5), .enable("false")) multiplexer_1 (
    .in0(\registrador_de_5_bits_1_saída ), .in1(\registrador_de_5_bits_2_saída ),
    .in2(\registrador_de_5_bits_3_saída ), .in3(\registrador_de_5_bits_4_saída ),
    .in4(\registrador_de_5_bits_5_saída ), .in5(\registrador_de_5_bits_6_saída ),
    .in6(\registrador_de_5_bits_7_saída ), .in7(\registrador_de_5_bits_8_saída ), .out(DataRegA), .sel(in_3));
  Multiplexer #(.select(3), .width(5), .enable("false")) multiplexer_2 (
    .in0(\registrador_de_5_bits_1_saída ), .in1(\registrador_de_5_bits_2_saída ),
    .in2(\registrador_de_5_bits_3_saída ), .in3(\registrador_de_5_bits_4_saída ),
    .in4(\registrador_de_5_bits_5_saída ), .in5(\registrador_de_5_bits_6_saída ),
    .in6(\registrador_de_5_bits_7_saída ), .in7(\registrador_de_5_bits_8_saída ), .out(DataRegB), .sel(in_5));
endmodule

module SRL_de_32_bits (
  input  [31:0] in_1,
  input  in_2,
  output [31:0] out_3
);

  Multiplexer #(.width(32), .enable("false")) multiplexer_1 (
    .in0(in_1), .in1({1'b0, in_1[31:1]}), .out(out_3), .sel(in_2));
endmodule

module SRA_de_32_Bits (
  input  [31:0] in_1,
  input  in_2,
  output [31:0] out_3
);

  Multiplexer #(.width(32), .enable("false")) multiplexer_1 (
    .in0(in_1), .in1({{2{in_1[31]}}, in_1[30:1]}), .out(out_3), .sel(in_2));
endmodule

module Subtrator_Completo (
  input  A,
  input  B,
  input  in_3,
  output Soma,
  output out_5
);

  wire and_1_out, and_2_out, and_3_out, xor_1_out;

  or or_1 (out_5, and_1_out, and_2_out, and_3_out);
  and and_1 (and_1_out, ~A, B);  // AND_Gate
  and and_2 (and_2_out, in_3, B);
  and and_3 (and_3_out, in_3, ~A);  // AND_Gate
  xor xor_1 (xor_1_out, A, B);
  xor xor_2 (Soma, in_3, xor_1_out);
endmodule

module LUA_32_Bits (
  input  [31:0] Entrada,
  input  Shift,
  output [31:0] Entrada_2
);

  Multiplexer #(.width(32), .enable("false")) multiplexer_1 (
    .in0(Entrada),
    .in1({Entrada[0], Entrada[1], Entrada[2], Entrada[3], Entrada[4], Entrada[5], Entrada[6], Entrada[7], Entrada[8], Entrada[9], Entrada[10], Entrada[11], Entrada[12], Entrada[13], Entrada[14], Entrada[15], {16{1'b0}}}),
    .out(Entrada_2), .sel(Shift));
endmodule

module SLL_detector (
  input  [3:0] OperCOde,
  output \Saída 
);

  and and_1 (\Saída , ~OperCOde[3], OperCOde[2], ~OperCOde[1], OperCOde[0]);  // AND_Gate
endmodule

module SRL_Detector (
  input  [3:0] OperCOde,
  output \Saída 
);

  and and_1 (\Saída , ~OperCOde[3], OperCOde[2], OperCOde[1], ~OperCOde[0]);  // AND_Gate
endmodule

module SRA_Detector (
  input  [3:0] OperCOde,
  output \Saída 
);

  and and_1 (\Saída , ~OperCOde[3], OperCOde[2], OperCOde[1], OperCOde[0]);  // AND_Gate
endmodule

module LUA_Detector (
  input  [3:0] OperCOde,
  output \Saída 
);

  and and_1 (\Saída , OperCOde[3], ~OperCOde[2], ~OperCOde[1], ~OperCOde[0]);  // AND_Gate
endmodule

module Via_de_Dados (
  input  WR,
  input  Reset,
  input  [4:0] Reg_W,
  input  [4:0] Reg_A,
  input  [4:0] Reg_B,
  input  [3:0] Opercode,
  input  [31:0] in_7,
  output [7:0] Addr
);

  wire not_1_out;
  wire [31:0] banco_de_registradores_1_datarega, banco_de_registradores_1_dataregb, multiplexer_1_out,
       n17_para_32_1_s, \ula_32_bits_1_saída ;

  not not_1 (not_1_out, WR);
  PC pc_1 (.Clk(not_1_out), .Reset(Reset), .Addr(Addr));
  Banco_de_Registradores banco_de_registradores_1 (
    .WR(WR), .Reset(Reset), .DataIn(\ula_32_bits_1_saída ), .SelRegW(Reg_W), .SelRegA(Reg_A),
    .SelRegB(Reg_B), .DataRegA(banco_de_registradores_1_datarega),
    .DataRegB(banco_de_registradores_1_dataregb));  // open: in_3, Data_in_Externo
  _17_para_32 u_17_para_32_1 (.E(in_7[17:1]), .S(n17_para_32_1_s));
  ULA_32_Bits ula_32_bits_1 (
    .A(banco_de_registradores_1_datarega), .B(multiplexer_1_out), .\Saída (\ula_32_bits_1_saída ),
    .Opercode(Opercode));
  Multiplexer #(.width(32), .enable("false")) multiplexer_1 (
    .in0(banco_de_registradores_1_dataregb), .in1(n17_para_32_1_s), .out(multiplexer_1_out), .sel(in_7[0]));

  // Other names for the same wires on the sheet: i = in_7[0]; Externo[11:0] = in_7[12:1]; Reg_B_t[4:0] = in_7[17:13];
  //   Reg_A_t[4:0] = in_7[22:18]; Reg_W_t[4:0] = in_7[27:23]; OperCode_t[3:0] = in_7[31:28]

  // Notes on the sheet:
  //   1080001F
  //   1103E001
  //   11844000
endmodule

module PC (
  input  Clk,
  input  Reset,
  output [7:0] Addr
);

  wire [7:0] adder_1_out;

  Adder adder_1 (.a(Addr), .b(8'h1), .out(adder_1_out));  // open: cin, cout
  Register register_1 (.D(adder_1_out), .Q(Addr), .clk(Clk), .clr(Reset));  // open: en
endmodule

module Computador (
  input  in_1,
  input  Reset
);

  wire [7:0] Addr;
  wire [31:0] via_de_dados_1_p3;

  // Via_de_Dados via_de_dados_1: pin names not known; wires that end beside it: in_1, Reset, via_de_dados_1_p3
  RAM #(.dataWidth(32)) ram_1 (.addr(Addr), .data(via_de_dados_1_p3), .clr(Reset));  // open: sel, clk, ld

  // Notes on the sheet:
  //   1080001F
  //   1103E001
  //   11844000
endmodule

module _17_para_32 (
  input  [16:0] E,
  output [31:0] S
);


  assign S = {{16{E[16]}}, E[15:0]};
endmodule

module SLL (
  input  [31:0] in_1
);
endmodule
